# Fritzing sketch PlayGate (saved by Fritzing 1.0.4)
breadboards: 1

parts:
  LED1 = LED - 5mm [color="Red (633nm)" current=0.030A package="5 mm [THT]"]
  LED2 = LED - 5mm [color="Red (633nm)" current=0.030A package="5 mm [THT]"]
  BUTTON_1 = KY-004 Key Switch Module [package="Breakout board"]
  BUTTON_2 = KY-004 Key Switch Module [package="Breakout board"]
  Pico_H1 = Raspberry Pi Pico H
  USB_to_TTL = USB converter CP2102

nets:
  GND: LED1.cathode, LED2.cathode, BUTTON_1.-, BUTTON_2.-, Pico_H1.GND, USB_to_TTL.GND
  N1: LED1.anode, Pico_H1.GP11
  N2: LED2.anode, Pico_H1.GP12
  N3: BUTTON_1.S, Pico_H1.GP15
  VIN: BUTTON_1.Vin, BUTTON_2.Vin
  N4: BUTTON_2.S, Pico_H1.GP14
  N5: Pico_H1.GP4, USB_to_TTL.3V3

custom parts:
  KY-004 Key Switch Module: Arduino Key Switch Module Keyes KY-004 is a push button that will output a high signal when pressed.
  Raspberry Pi Pico H: Raspberry Pi Pico H. Based around the RP2040 microcontroller the Pico H is a low cost microcontroller device bringing Raspberry Pi quality, cost, and easy of use to the microcontroller space.
